// Logisim project ex4.circ as structural Verilog: 5 circuits, main circuit RotRight
module RotRight (
  input  [15:0] INPUT0,
  input  [3:0] AMOUNT,
  output [15:0] OUTPUT0
);

  wire bitselector_1_out, bitselector_2_out, bitselector_3_out, bitselector_4_out;
  wire [15:0] multiplexer_1_out, multiplexer_2_out, multiplexer_3_out, multiplexer_4_out, multiplexer_5_out,
       multiplexer_6_out, multiplexer_7_out, rot1_1_out_2, rot2_1_out_2, rot4_1_out_2, rot8_1_out_2;

  BitSelector #(.width(4)) bitselector_1 (.in(AMOUNT), .out(bitselector_1_out), .sel(2'b00));
  BitSelector #(.width(4)) bitselector_2 (.in(AMOUNT), .out(bitselector_2_out), .sel(2'b01));
  BitSelector #(.width(4)) bitselector_3 (.in(AMOUNT), .out(bitselector_3_out), .sel(2'b10));
  BitSelector #(.width(4)) bitselector_4 (.in(AMOUNT), .out(bitselector_4_out), .sel(2'b11));
  Multiplexer #(.width(16)) multiplexer_1 (
    .in0({16{1'b0}}), .in1(INPUT0), .out(multiplexer_1_out), .sel(bitselector_1_out));
  Multiplexer #(.width(16)) multiplexer_2 (
    .in0({16{1'b0}}), .in1(multiplexer_5_out), .out(multiplexer_2_out), .sel(bitselector_2_out));
  Multiplexer #(.width(16)) multiplexer_3 (
    .in0({16{1'b0}}), .in1(multiplexer_6_out), .out(multiplexer_3_out), .sel(bitselector_3_out));
  Multiplexer #(.width(16)) multiplexer_4 (
    .in0({16{1'b0}}), .in1(multiplexer_7_out), .out(multiplexer_4_out), .sel(bitselector_4_out));
  rot1 rot1_1 (.in_1(multiplexer_1_out), .out_2(rot1_1_out_2));
  Multiplexer #(.width(16)) multiplexer_5 (
    .in0(INPUT0), .in1(rot1_1_out_2), .out(multiplexer_5_out), .sel(bitselector_1_out));
  Multiplexer #(.width(16)) multiplexer_6 (
    .in0(multiplexer_5_out), .in1(rot2_1_out_2), .out(multiplexer_6_out), .sel(bitselector_2_out));
  Multiplexer #(.width(16)) multiplexer_7 (
    .in0(multiplexer_6_out), .in1(rot4_1_out_2), .out(multiplexer_7_out), .sel(bitselector_3_out));
  Multiplexer #(.width(16)) multiplexer_8 (
    .in0(multiplexer_7_out), .in1(rot8_1_out_2), .out(OUTPUT0), .sel(bitselector_4_out));
  rot2 rot2_1 (.in_1(multiplexer_2_out), .out_2(rot2_1_out_2));
  rot4 rot4_1 (.in_1(multiplexer_3_out), .out_2(rot4_1_out_2));
  rot8 rot8_1 (.in_1(multiplexer_4_out), .out_2(rot8_1_out_2));
endmodule

module rot1 (
  input  [15:0] in_1,
  output [15:0] out_2
);


  assign out_2 = {in_1[0], in_1[15:1]};
endmodule

module rot2 (
  input  [15:0] in_1,
  output [15:0] out_2
);


  assign out_2 = {in_1[1:0], in_1[15:2]};
endmodule

module rot4 (
  input  [15:0] in_1,
  output [15:0] out_2
);


  assign out_2 = {in_1[3:0], in_1[15:4]};
endmodule

module rot8 (
  input  [15:0] in_1,
  output [15:0] out_2
);


  assign out_2 = {in_1[7:0], in_1[15:8]};
endmodule
