// Logisim project branch-comp.circ as structural Verilog: 1 circuit, main circuit branch_comp
module branch_comp (
  input  [31:0] BrData1,
  input  [31:0] BrData2,
  input  BrUn,
  output BrEq,
  output BrLt
);

  wire Sign_Breq, Sign_BrLt, UnSign_Breq, UnSign_BrLt;

  Comparator #(.width(32)) comparator_1 (.a(BrData1), .b(BrData2), .eq(Sign_Breq), .lt(Sign_BrLt));  // open: gt
  Comparator #(.mode("unsigned"), .width(32)) comparator_2 (
    .a(BrData1), .b(BrData2), .eq(UnSign_Breq), .lt(UnSign_BrLt));  // open: gt
  Multiplexer multiplexer_1 (.in0(Sign_Breq), .in1(UnSign_Breq), .out(BrEq), .sel(BrUn));
  Multiplexer multiplexer_2 (.in0(Sign_BrLt), .in1(UnSign_BrLt), .out(BrLt), .sel(BrUn));

  // Notes on the sheet:
  //   INPUTS to your circuit
  //   DON'T CHANGE THE LOCATIONS OF THE INPUTS AND OUTPUTS!
  //   OUTPUT from your circuit
endmodule
