// Logisim project control-logic.circ as structural Verilog: 1 circuit, main circuit control_logic
module control_logic (
  input  [31:0] Instruction,
  input  BrEq,
  input  BrLt,
  output PCSel,
  output RegWEn,
  output [2:0] ImmSel,
  output BrUn,
  output ASel,
  output BSel,
  output [3:0] ALUSel,
  output MemRW,
  output [1:0] WBSel
);

  wire and_24_out, and_25_out, and_26_out, and_27_out, auipc, B_Format, fun3_000, fun3_001, fun3_010,
       fun3_011, fun3_100, fun3_101, fun3_110, fun3_111, fun7_0000000, fun7_0000001, fun7_0100000,
       Imm_Format, is_add, is_addi, is_and, is_andi, is_beq, is_bge, is_bgeu, is_blt, is_bltu, is_bne, is_lb,
       is_lh, is_lw, is_mul, is_mulh, is_mulhu, is_or, is_ori, is_sb, is_sh, is_sll, is_slli, is_slt,
       is_slti, is_sra, is_srai, is_srl, is_srli, is_sub, is_sw, is_xor, is_xori, jal, jalr, Load_Format,
       lui, not_1_out, not_2_out, or_1_out, or_2_out, R_Format, S_Format;
  wire [5:0] ROM_Input;
  wire [15:14] rom_1_data;

  Comparator #(.width(3)) comparator_1 (.a(Instruction[14:12]), .b(3'b000), .eq(fun3_000));  // open: gt, lt
  Comparator #(.width(3)) comparator_2 (.a(Instruction[14:12]), .b(3'b001), .eq(fun3_001));  // open: gt, lt
  Comparator #(.width(3)) comparator_3 (.a(Instruction[14:12]), .b(3'b010), .eq(fun3_010));  // open: gt, lt
  Comparator #(.width(3)) comparator_4 (.a(Instruction[14:12]), .b(3'b011), .eq(fun3_011));  // open: gt, lt
  Comparator #(.width(3)) comparator_5 (.a(Instruction[14:12]), .b(3'b100), .eq(fun3_100));  // open: gt, lt
  Comparator #(.width(3)) comparator_6 (.a(Instruction[14:12]), .b(3'b101), .eq(fun3_101));  // open: gt, lt
  Comparator #(.width(3)) comparator_7 (.a(Instruction[14:12]), .b(3'b110), .eq(fun3_110));  // open: gt, lt
  Comparator #(.width(3)) comparator_8 (.a(Instruction[14:12]), .b(3'b111), .eq(fun3_111));  // open: gt, lt
  ROM #(.addrWidth(6), .dataWidth(16)) rom_1 (
    .addr(ROM_Input), .data({rom_1_data, WBSel, MemRW, ALUSel, BSel, ASel, BrUn, ImmSel, RegWEn}));
  and and_1 (is_add, R_Format, fun3_000, fun7_0000000);
  and and_2 (is_mul, R_Format, fun3_000, fun7_0000001);
  and and_3 (is_sub, R_Format, fun3_000, fun7_0100000);
  and and_4 (is_sll, R_Format, fun3_001, fun7_0000000);
  and and_5 (is_mulh, R_Format, fun3_001, fun7_0000001);
  and and_6 (is_mulhu, R_Format, fun3_011, fun7_0000001);
  and and_7 (is_slt, R_Format, fun3_010, fun7_0000000);
  and and_8 (is_xor, R_Format, fun3_100, fun7_0000000);
  and and_9 (is_srl, R_Format, fun3_101, fun7_0000000);
  and and_10 (is_sra, R_Format, fun3_101, fun7_0100000);
  and and_11 (is_or, R_Format, fun3_110, fun7_0000000);
  and and_12 (is_and, R_Format, fun3_111, fun7_0000000);
  Comparator #(.width(7)) comparator_9 (.a(Instruction[6:0]), .b(7'b0110011), .eq(R_Format));  // open: gt, lt
  Comparator #(.width(7)) comparator_10 (.a(Instruction[6:0]), .b(7'b0000011), .eq(Load_Format));  // open: gt, lt
  Comparator #(.width(7)) comparator_11 (.a(Instruction[6:0]), .b(7'b0010011), .eq(Imm_Format));  // open: gt, lt
  Comparator #(.width(7)) comparator_12 (.a(Instruction[6:0]), .b(7'b0100011), .eq(S_Format));  // open: gt, lt
  Comparator #(.width(7)) comparator_13 (.a(Instruction[6:0]), .b(7'b1100011), .eq(B_Format));  // open: gt, lt
  Comparator #(.width(7)) comparator_14 (.a(Instruction[6:0]), .b(7'b0010111), .eq(auipc));  // open: gt, lt
  Comparator #(.width(7)) comparator_15 (.a(Instruction[6:0]), .b(7'b0110111), .eq(lui));  // open: gt, lt
  Comparator #(.width(7)) comparator_16 (.a(Instruction[6:0]), .b(7'b1101111), .eq(jal));  // open: gt, lt
  Comparator #(.width(7)) comparator_17 (.a(Instruction[6:0]), .b(7'b1100111), .eq(jalr));  // open: gt, lt
  Comparator #(.width(7)) comparator_18 (.a(Instruction[31:25]), .b({7{1'b0}}), .eq(fun7_0000000));  // open: gt, lt
  Comparator #(.width(7)) comparator_19 (.a(Instruction[31:25]), .b(7'b0000001), .eq(fun7_0000001));  // open: gt, lt
  Comparator #(.width(7)) comparator_20 (.a(Instruction[31:25]), .b(7'b0100000), .eq(fun7_0100000));  // open: gt, lt
  and and_13 (is_lb, Load_Format, fun3_000);
  and and_14 (is_lh, Load_Format, fun3_001);
  and and_15 (is_lw, Load_Format, fun3_010);
  and and_16 (is_addi, Imm_Format, fun3_000);
  and and_17 (is_slli, Imm_Format, fun3_001, fun7_0000000);
  and and_18 (is_slti, Imm_Format, fun3_010);
  and and_19 (is_xori, Imm_Format, fun3_100);
  and and_20 (is_srli, Imm_Format, fun3_101, fun7_0000000);
  and and_21 (is_srai, Imm_Format, fun3_101, fun7_0100000);
  and and_22 (is_ori, Imm_Format, fun3_110);
  and and_23 (is_andi, Imm_Format, fun3_111);
  or or_1 (or_1_out, is_blt, is_bltu);
  or or_2 (or_2_out, is_bge, is_bgeu);
  not not_1 (not_1_out, BrEq);
  not not_2 (not_2_out, BrLt);
  and and_24 (and_24_out, is_beq, BrEq);
  and and_25 (and_25_out, not_1_out, is_bne);
  and and_26 (and_26_out, or_1_out, BrLt);
  and and_27 (and_27_out, not_2_out, or_2_out);
  and and_28 (is_sb, S_Format, fun3_000);
  and and_29 (is_sh, S_Format, fun3_001);
  and and_30 (is_sw, S_Format, fun3_010);
  and and_31 (is_beq, B_Format, fun3_000);
  and and_32 (is_bne, B_Format, fun3_001);
  and and_33 (is_blt, B_Format, fun3_100);
  and and_34 (is_bge, B_Format, fun3_101);
  and and_35 (is_bltu, B_Format, fun3_110);
  and and_36 (is_bgeu, B_Format, fun3_111);
  or or_3 (PCSel, jal, and_24_out, and_25_out, and_26_out, and_27_out, jalr);
  // Priority_Encoder #(.select_enc(6)) priority_encoder_1: pin names not known; wires that end beside it: ROM_Input, is_add, is_mul, is_sub, is_sll, is_mulh, is_mulhu, is_slt, is_xor, is_srl, is_sra, is_or, is_and, is_lb, is_lh, is_lw, is_addi, is_slli, is_slti, is_xori, is_srli, is_srai, is_ori, is_andi, is_sb, is_sh, is_sw, is_beq, is_bne, is_blt, is_bge, is_bltu, is_bgeu, auipc, lui, jal, jalr

  // Other names for the same wires on the sheet: Opcode[6:0] = Instruction[6:0]; bit_7_11[4:0] = Instruction[11:7];
  //   bit_12_14[2:0] = Instruction[14:12]; bit_15_19[4:0] = Instruction[19:15]; bit_20_24[4:0] = Instruction[24:20];
  //   bit_25_31[6:0] = Instruction[31:25]

  // Notes on the sheet:
  //   INPUTS to your circuit
  //   Connect ROM Input here ->
  //   contents of rom_1 (hex, n*v repeats v):
  //   100f 140f 160f 108f 148f 158f 110f 120f 128f 168f 130f 13cf 41 41 41 1041 10c1 1141 1241 12c1 16c1
  //   1341 13c1 1043 1043 1043 4*1064 1074 1074 1067 17e7 2069 2041
  //   ROM FOR CONTROL LOGIC
  //   DON'T CHANGE THE LOCATIONS OF THE INPUTS AND OUTPUTS!
  //   This is only if you choose to do the ROM option
  //   CONNECT
  //   WIRE
  //   TO
  //   USE
  //   ROM
  //   OUTPUT from your circuit
  //   Reminder: If using ROM, use combinational logic for PCSel
  //   Attention: Only B_format is true can't decide the PCSel.
  //   PCSel is token only when it's B-format and according condition is true and j format
endmodule
