// Logisim project imm-gen.circ as structural Verilog: 1 circuit, main circuit imm_gen
module imm_gen (
  input  [31:0] Instruction,
  input  [2:0] ImmSel,
  output [31:0] Immediate
);

  wire [31:0] B_imm, I_imm, J_imm, S_imm, U_imm;

  assign I_imm = {{20{Instruction[31]}}, Instruction[31:20]};  // Bit_Extender bit_extender_1
  assign S_imm = {{20{Instruction[31]}}, {Instruction[31:25], Instruction[11:7]}};  // Bit_Extender bit_extender_2
  assign B_imm = {{19{Instruction[31]}}, {Instruction[31], Instruction[7], Instruction[30:25], Instruction[11:8], 1'b0}};  // Bit_Extender bit_extender_3
  assign U_imm = {{12{Instruction[31]}}, Instruction[31:12]};  // Bit_Extender bit_extender_4
  assign J_imm = {{11{Instruction[31]}}, {Instruction[31], Instruction[19:12], Instruction[20], Instruction[30:21], 1'b0}};  // Bit_Extender bit_extender_5
  Multiplexer #(.select(3), .width(32)) multiplexer_1 (
    .in0(I_imm), .in1(S_imm), .in2(B_imm), .in3(U_imm), .in4(J_imm), .out(Immediate), .sel(ImmSel));  // open: in5, in6, in7

  // Notes on the sheet:
  //   INPUTS to your circuit
  //   DON'T CHANGE THE LOCATIONS OF THE INPUTS AND OUTPUTS!
  //   OUTPUT from your circuit
endmodule
