// Logisim project partial-load.circ as structural Verilog: 1 circuit, main circuit partial_load
module partial_load (
  input  [31:0] Instruction,
  input  [31:0] MemAddress,
  input  [31:0] DataFromMem,
  output [31:0] DataToReg
);

  wire E7_0, E15_0, E15_8, E23_8, E23_16, E31_16, E31_24, f3_0, f3_1, f3_11, full32, is_00, is_01, is_10,
       is_11, is_Load, lb, lh, lw;
  wire [2:0] SignEXT_type;
  wire [31:0] EXT7_0, EXT15_0, EXT15_8, EXT23_8, EXT23_16, EXT31_16, EXT31_24;

  Comparator #(.width(7)) comparator_1 (.a(Instruction[6:0]), .b(7'b0000011), .eq(is_Load));  // open: gt, lt
  Comparator #(.width(3)) comparator_2 (.a(Instruction[14:12]), .b(3'b000), .eq(f3_0));  // open: gt, lt
  Comparator #(.width(3)) comparator_3 (.a(Instruction[14:12]), .b(3'b001), .eq(f3_1));  // open: gt, lt
  Comparator #(.width(3)) comparator_4 (.a(Instruction[14:12]), .b(3'b010), .eq(f3_11));  // open: gt, lt
  and and_1 (lb, is_Load, f3_0);
  and and_2 (lh, is_Load, f3_1);
  and and_3 (lw, is_Load, f3_11);
  and and_4 (E7_0, lb, is_00);
  and and_5 (E15_8, lb, is_01);
  and and_6 (E23_16, lb, is_10);
  and and_7 (E31_24, lb, is_11);
  Comparator #(.width(2)) comparator_5 (.a(MemAddress[1:0]), .b(2'b00), .eq(is_00));  // open: gt, lt
  Comparator #(.width(2)) comparator_6 (.a(MemAddress[1:0]), .b(2'b01), .eq(is_01));  // open: gt, lt
  Comparator #(.width(2)) comparator_7 (.a(MemAddress[1:0]), .b(2'b10), .eq(is_10));  // open: gt, lt
  Comparator #(.width(2)) comparator_8 (.a(MemAddress[1:0]), .b(2'b11), .eq(is_11));  // open: gt, lt
  and and_8 (E15_0, lh, is_00);
  and and_9 (E23_8, lh, is_01);
  and and_10 (E31_16, lh, is_10);
  and and_11 (full32, lw, is_00);
  Multiplexer #(.select(3), .width(32)) multiplexer_1 (
    .in0(EXT7_0), .in1(EXT15_8), .in2(EXT23_16), .in3(EXT31_24), .in4(EXT15_0), .in5(EXT23_8),
    .in6(EXT31_16), .in7(DataFromMem), .out(DataToReg), .sel(SignEXT_type));
  Priority_Encoder priority_encoder_1 (
    .in0(E7_0), .in1(E15_8), .in2(E23_16), .in3(E31_24), .in4(E15_0), .in5(E23_8), .in6(E31_16),
    .in7(full32), .out(SignEXT_type));  // open: en_in, gs, en_out
  assign EXT7_0 = {{24{DataFromMem[7]}}, DataFromMem[7:0]};  // Bit_Extender bit_extender_1
  assign EXT15_8 = {{24{DataFromMem[15]}}, DataFromMem[15:8]};  // Bit_Extender bit_extender_2
  assign EXT23_16 = {{24{DataFromMem[23]}}, DataFromMem[23:16]};  // Bit_Extender bit_extender_3
  assign EXT31_24 = {{24{DataFromMem[31]}}, DataFromMem[31:24]};  // Bit_Extender bit_extender_4
  assign EXT15_0 = {{16{DataFromMem[15]}}, DataFromMem[15:0]};  // Bit_Extender bit_extender_5
  assign EXT23_8 = {{16{DataFromMem[23]}}, DataFromMem[23:8]};  // Bit_Extender bit_extender_6
  assign EXT31_16 = {{16{DataFromMem[31]}}, DataFromMem[31:16]};  // Bit_Extender bit_extender_7

  // Other names for the same wires on the sheet: bit7_0[7:0] = DataFromMem[7:0]; bit15_0[15:0] = DataFromMem[15:0];
  //   bit15_8[7:0] = DataFromMem[15:8]; bit23_8[15:0] = DataFromMem[23:8]; bit23_16[7:0] = DataFromMem[23:16];
  //   bit31_16[15:0] = DataFromMem[31:16]; bit31_24[7:0] = DataFromMem[31:24]; opcode[6:0] = Instruction[6:0];
  //   fun3_in_load[2:0] = Instruction[14:12]; Bottom_2_bits[1:0] = MemAddress[1:0]

  // Notes on the sheet:
  //   INPUTS to your circuit
  //   get the type of the load instruction
  //   Split the instruction
  //   DON'T CHANGE THE LOCATIONS OF THE INPUTS AND OUTPUTS!
  //   get bottom 2 bits
  //   OUTPUT from your circuit
  //   get SignEXT type
  //   mapping
  //   get bits
  //   sign_EXT
endmodule
