// Logisim project partial-store.circ as structural Verilog: 1 circuit, main circuit partial_store
module partial_store (
  input  [31:0] Instruction,
  input  [31:0] MemAddress,
  input  [31:0] DataFromReg,
  input  MemRW,
  output [3:0] MemWriteMask,
  output [31:0] DataToMem
);

  wire E7_0, E15_0, E15_8, E23_16, E31_16, E31_24, f3_s_0, f3_s_1, f3_s_2, full32, is_00, is_01, is_10,
       is_11, is_Store, not_1_out, sb, sh, sw;
  wire [2:0] Str_Sel, which_s;
  wire [31:0] result_of_byte, result_of_half;

  Comparator #(.width(7)) comparator_1 (.a(Instruction[6:0]), .b(7'b0100011), .eq(is_Store));  // open: gt, lt
  Comparator #(.width(3)) comparator_2 (.a(Instruction[14:12]), .b(3'b000), .eq(f3_s_0));  // open: gt, lt
  Comparator #(.width(3)) comparator_3 (.a(Instruction[14:12]), .b(3'b001), .eq(f3_s_1));  // open: gt, lt
  Comparator #(.width(3)) comparator_4 (.a(Instruction[14:12]), .b(3'b010), .eq(f3_s_2));  // open: gt, lt
  and and_1 (sb, is_Store, f3_s_0);
  and and_2 (sh, is_Store, f3_s_1);
  and and_3 (sw, is_Store, f3_s_2);
  and and_4 (E7_0, sb, is_00);
  and and_5 (E15_8, sb, is_01);
  and and_6 (E23_16, sb, is_10);
  and and_7 (E31_24, sb, is_11);
  Comparator #(.width(2)) comparator_5 (.a(MemAddress[1:0]), .b(2'b00), .eq(is_00));  // open: gt, lt
  Comparator #(.width(2)) comparator_6 (.a(MemAddress[1:0]), .b(2'b01), .eq(is_01));  // open: gt, lt
  Comparator #(.width(2)) comparator_7 (.a(MemAddress[1:0]), .b(2'b10), .eq(is_10));  // open: gt, lt
  Comparator #(.width(2)) comparator_8 (.a(MemAddress[1:0]), .b(2'b11), .eq(is_11));  // open: gt, lt
  and and_8 (E15_0, sh, is_00);
  and and_9 (E31_16, sh, is_10);
  and and_10 (full32, sw, is_00);
  Priority_Encoder priority_encoder_1 (
    .in0(sb), .in1(sh), .in2(sw), .out(which_s));  // open: in3, in4, in5, in6, in7, en_in, gs, en_out
  not not_1 (not_1_out, MemRW);
  Priority_Encoder priority_encoder_2 (
    .in0(E7_0), .in1(E15_8), .in2(E23_16), .in3(E31_24), .in4(E15_0), .in5(E31_16), .in6(full32),
    .out(Str_Sel));  // open: in7, en_in, gs, en_out
  Priority_Encoder #(.select_enc(4)) priority_encoder_3 (
    .in0(not_1_out), .in1(E7_0), .in2(E15_8), .in3(E15_0), .in4(E23_16), .in8(E31_24), .in12(E31_16),
    .in15(full32), .out(MemWriteMask));  // open: in5, in6, in7, in9, in10, in11, in13, in14, gs, en_out, en_in
  Multiplexer #(.select(2), .width(32)) multiplexer_1 (
    .in0({{24{1'b0}}, DataFromReg[7:0]}), .in1({{16{1'b0}}, DataFromReg[7:0], {8{1'b0}}}),
    .in2({{8{1'b0}}, DataFromReg[7:0], {16{1'b0}}}), .in3({DataFromReg[7:0], {24{1'b0}}}),
    .out(result_of_byte), .sel(MemAddress[1:0]));
  Multiplexer #(.select(2), .width(32)) multiplexer_2 (
    .in0({{16{1'b0}}, DataFromReg[15:0]}), .in2({DataFromReg[15:0], {16{1'b0}}}), .out(result_of_half),
    .sel(MemAddress[1:0]));  // open: in1, in3
  Multiplexer #(.select(3), .width(32)) multiplexer_3 (
    .in0(result_of_byte), .in1(result_of_half), .in2(DataFromReg), .out(DataToMem), .sel(which_s));  // open: in3, in4, in5, in6, in7

  // Other names for the same wires on the sheet: bit23_16[7:0] = DataFromReg[23:16];
  //   bit31_16[15:0] = DataFromReg[31:16]; bit31_24[7:0] = DataFromReg[31:24]; bit7_0[7:0] = DataFromReg[7:0];
  //   bit15_0[15:0] = DataFromReg[15:0]; EXT_index0[7:0] = DataFromReg[7:0]; EXT_index0_1[15:0] = DataFromReg[15:0];
  //   EXT_index1[15:8] = DataFromReg[7:0]; EXT_index2[23:16] = DataFromReg[7:0];
  //   EXT_index2_3[31:16] = DataFromReg[15:0]; EXT_index3[31:24] = DataFromReg[7:0]; bit15_8[7:0] = DataFromReg[15:8];
  //   opcode[6:0] = Instruction[6:0]; fun3_in_store[2:0] = Instruction[14:12]; Bottom_2_bits[1:0] = MemAddress[1:0]

  // Notes on the sheet:
  //   INPUTS to your circuit
  //   get the type of the load instruction
  //   Split the instruction
  //   get bottom 2 bits
  //   get SignEXT type
  //   DON'T CHANGE THE LOCATIONS OF THE INPUTS AND OUTPUTS!
  //   OUTPUT from your circuit
  //   mapping
  //   get bits
  //   sign_EXT
  //   select which extended number should be written to memory
endmodule
