// Logisim project regfile.circ as structural Verilog: 1 circuit, main circuit regfile
module regfile (
  input  [4:0] ReadIndex1,
  input  [4:0] ReadIndex2,
  input  [4:0] WriteIndex,
  input  [31:0] WriteData,
  input  RegWEn,
  input  clk,
  output [31:0] ra,
  output [31:0] sp,
  output [31:0] t0,
  output [31:0] t1,
  output [31:0] t2,
  output [31:0] s0,
  output [31:0] s1,
  output [31:0] a0,
  output [31:0] ReadData1,
  output [31:0] ReadData2
);

  wire comparator_1_eq, comparator_2_eq, comparator_3_eq, comparator_4_eq, comparator_5_eq, comparator_6_eq,
       comparator_7_eq, comparator_8_eq, comparator_9_eq, comparator_10_eq, comparator_11_eq,
       comparator_12_eq, comparator_13_eq, comparator_14_eq, comparator_15_eq, comparator_16_eq,
       comparator_17_eq, comparator_18_eq, comparator_19_eq, comparator_20_eq, comparator_21_eq,
       comparator_22_eq, comparator_23_eq, comparator_24_eq, comparator_25_eq, comparator_26_eq,
       comparator_27_eq, comparator_28_eq, comparator_29_eq, comparator_30_eq, comparator_31_eq,
       comparator_32_eq, not_1_out;
  wire [31:0] bit_extender_1_out, demultiplexer_1_out0, demultiplexer_1_out1, demultiplexer_2_out0,
       demultiplexer_2_out1, demultiplexer_3_out0, demultiplexer_3_out1, demultiplexer_4_out0,
       demultiplexer_4_out1, demultiplexer_5_out0, demultiplexer_5_out1, demultiplexer_6_out0,
       demultiplexer_6_out1, demultiplexer_7_out0, demultiplexer_7_out1, demultiplexer_8_out0,
       demultiplexer_8_out1, demultiplexer_9_out0, demultiplexer_9_out1, demultiplexer_10_out0,
       demultiplexer_10_out1, demultiplexer_11_out0, demultiplexer_11_out1, demultiplexer_12_out0,
       demultiplexer_12_out1, demultiplexer_13_out0, demultiplexer_13_out1, demultiplexer_14_out0,
       demultiplexer_14_out1, demultiplexer_15_out0, demultiplexer_15_out1, demultiplexer_16_out0,
       demultiplexer_16_out1, demultiplexer_17_out0, demultiplexer_17_out1, demultiplexer_18_out0,
       demultiplexer_18_out1, demultiplexer_19_out0, demultiplexer_19_out1, demultiplexer_20_out0,
       demultiplexer_20_out1, demultiplexer_21_out0, demultiplexer_21_out1, demultiplexer_22_out0,
       demultiplexer_22_out1, demultiplexer_23_out0, demultiplexer_23_out1, demultiplexer_24_out0,
       demultiplexer_24_out1, demultiplexer_25_out0, demultiplexer_25_out1, demultiplexer_26_out0,
       demultiplexer_26_out1, demultiplexer_27_out0, demultiplexer_27_out1, demultiplexer_28_out0,
       demultiplexer_28_out1, demultiplexer_29_out0, demultiplexer_29_out1, demultiplexer_30_out0,
       demultiplexer_30_out1, demultiplexer_31_out0, demultiplexer_31_out1;

  Comparator #(.width(5)) comparator_1 (.a({5{1'b0}}), .b(ReadIndex1), .eq(comparator_1_eq));  // open: gt, lt
  Comparator #(.width(5)) comparator_2 (.a(5'b00001), .b(ReadIndex1), .eq(comparator_2_eq));  // open: gt, lt
  Comparator #(.width(5)) comparator_3 (.a(5'b00010), .b(ReadIndex1), .eq(comparator_3_eq));  // open: gt, lt
  Comparator #(.width(5)) comparator_4 (.a(5'b00011), .b(ReadIndex1), .eq(comparator_4_eq));  // open: gt, lt
  Comparator #(.width(5)) comparator_5 (.a(5'b00100), .b(ReadIndex1), .eq(comparator_5_eq));  // open: gt, lt
  Comparator #(.width(5)) comparator_6 (.a(5'b00101), .b(ReadIndex1), .eq(comparator_6_eq));  // open: gt, lt
  Comparator #(.width(5)) comparator_7 (.a(5'b00110), .b(ReadIndex1), .eq(comparator_7_eq));  // open: gt, lt
  Comparator #(.width(5)) comparator_8 (.a(5'b00111), .b(ReadIndex1), .eq(comparator_8_eq));  // open: gt, lt
  not not_1 (not_1_out, comparator_1_eq);
  Demultiplexer #(.width(32)) demultiplexer_1 (
    .out0(demultiplexer_1_out0), .out1(demultiplexer_1_out1), .in(WriteData), .sel(comparator_2_eq));
  Demultiplexer #(.width(32)) demultiplexer_2 (
    .out0(demultiplexer_2_out0), .out1(demultiplexer_2_out1), .in(WriteData), .sel(comparator_3_eq));
  Demultiplexer #(.width(32)) demultiplexer_3 (
    .out0(demultiplexer_3_out0), .out1(demultiplexer_3_out1), .in(WriteData), .sel(comparator_4_eq));
  Demultiplexer #(.width(32)) demultiplexer_4 (
    .out0(demultiplexer_4_out0), .out1(demultiplexer_4_out1), .in(WriteData), .sel(comparator_5_eq));
  Demultiplexer #(.width(32)) demultiplexer_5 (
    .out0(demultiplexer_5_out0), .out1(demultiplexer_5_out1), .in(WriteData), .sel(comparator_6_eq));
  Demultiplexer #(.width(32)) demultiplexer_6 (
    .out0(demultiplexer_6_out0), .out1(demultiplexer_6_out1), .in(WriteData), .sel(comparator_7_eq));
  Demultiplexer #(.width(32)) demultiplexer_7 (
    .out0(demultiplexer_7_out0), .out1(demultiplexer_7_out1), .in(WriteData), .sel(comparator_8_eq));
  assign bit_extender_1_out = {{31{1'b0}}, not_1_out};  // Bit_Extender bit_extender_1
  Register #(.width(32)) x0 (.D(bit_extender_1_out), .en(RegWEn), .clk(clk));  // open: Q, clr
  // NoConnect on demultiplexer_1_out0
  Register #(.width(32)) x1 (.D(demultiplexer_1_out1), .en(RegWEn), .clk(clk), .Q(ReadData1));  // open: clr
  // NoConnect on demultiplexer_2_out0
  Register #(.width(32)) x2 (.D(demultiplexer_2_out1), .en(RegWEn), .clk(clk), .Q(ReadData1));  // open: clr
  // NoConnect on demultiplexer_3_out0
  Register #(.width(32)) x3 (.D(demultiplexer_3_out1), .en(RegWEn), .clk(clk), .Q(ReadData1));  // open: clr
  // NoConnect on demultiplexer_4_out0
  Register #(.width(32)) x4 (.D(demultiplexer_4_out1), .en(RegWEn), .clk(clk), .Q(ReadData1));  // open: clr
  // NoConnect on demultiplexer_5_out0
  Register #(.width(32)) x5 (.D(demultiplexer_5_out1), .en(RegWEn), .clk(clk), .Q(ReadData1));  // open: clr
  // NoConnect on demultiplexer_6_out0
  Register #(.width(32)) x6 (.D(demultiplexer_6_out1), .en(RegWEn), .clk(clk), .Q(ReadData1));  // open: clr
  // NoConnect on demultiplexer_7_out0
  Register #(.width(32)) x7 (.D(demultiplexer_7_out1), .en(RegWEn), .clk(clk), .Q(ReadData1));  // open: clr
  Comparator #(.width(5)) comparator_9 (.a(5'b01111), .b(ReadIndex1), .eq(comparator_9_eq));  // open: gt, lt
  Comparator #(.width(5)) comparator_10 (.a(5'b01110), .b(ReadIndex1), .eq(comparator_10_eq));  // open: gt, lt
  Comparator #(.width(5)) comparator_11 (.a(5'b01101), .b(ReadIndex1), .eq(comparator_11_eq));  // open: gt, lt
  Comparator #(.width(5)) comparator_12 (.a(5'b01100), .b(ReadIndex1), .eq(comparator_12_eq));  // open: gt, lt
  Comparator #(.width(5)) comparator_13 (.a(5'b01011), .b(ReadIndex1), .eq(comparator_13_eq));  // open: gt, lt
  Comparator #(.width(5)) comparator_14 (.a(5'b01010), .b(ReadIndex1), .eq(comparator_14_eq));  // open: gt, lt
  Comparator #(.width(5)) comparator_15 (.a(5'b01001), .b(ReadIndex1), .eq(comparator_15_eq));  // open: gt, lt
  Comparator #(.width(5)) comparator_16 (.a(5'b01000), .b(ReadIndex1), .eq(comparator_16_eq));  // open: gt, lt
  Demultiplexer #(.width(32)) demultiplexer_8 (
    .out0(demultiplexer_8_out0), .out1(demultiplexer_8_out1), .in(WriteData), .sel(comparator_9_eq));
  Demultiplexer #(.width(32)) demultiplexer_9 (
    .out0(demultiplexer_9_out0), .out1(demultiplexer_9_out1), .in(WriteData), .sel(comparator_10_eq));
  Demultiplexer #(.width(32)) demultiplexer_10 (
    .out0(demultiplexer_10_out0), .out1(demultiplexer_10_out1), .in(WriteData), .sel(comparator_11_eq));
  Demultiplexer #(.width(32)) demultiplexer_11 (
    .out0(demultiplexer_11_out0), .out1(demultiplexer_11_out1), .in(WriteData), .sel(comparator_12_eq));
  Demultiplexer #(.width(32)) demultiplexer_12 (
    .out0(demultiplexer_12_out0), .out1(demultiplexer_12_out1), .in(WriteData), .sel(comparator_13_eq));
  Demultiplexer #(.width(32)) demultiplexer_13 (
    .out0(demultiplexer_13_out0), .out1(demultiplexer_13_out1), .in(WriteData), .sel(comparator_14_eq));
  Demultiplexer #(.width(32)) demultiplexer_14 (
    .out0(demultiplexer_14_out0), .out1(demultiplexer_14_out1), .in(WriteData), .sel(comparator_15_eq));
  Demultiplexer #(.width(32)) demultiplexer_15 (
    .out0(demultiplexer_15_out0), .out1(demultiplexer_15_out1), .in(WriteData), .sel(comparator_16_eq));
  // NoConnect on demultiplexer_8_out0
  // NoConnect on demultiplexer_9_out0
  // NoConnect on demultiplexer_10_out0
  // NoConnect on demultiplexer_11_out0
  // NoConnect on demultiplexer_12_out0
  // NoConnect on demultiplexer_13_out0
  // NoConnect on demultiplexer_14_out0
  // NoConnect on demultiplexer_15_out0
  Register #(.width(32)) x15 (.D(demultiplexer_8_out1), .en(RegWEn), .clk(clk), .Q(ReadData1));  // open: clr
  Register #(.width(32)) x14 (.D(demultiplexer_9_out1), .en(RegWEn), .clk(clk), .Q(ReadData1));  // open: clr
  Register #(.width(32)) x13 (.D(demultiplexer_10_out1), .en(RegWEn), .clk(clk), .Q(ReadData1));  // open: clr
  Register #(.width(32)) x12 (.D(demultiplexer_11_out1), .en(RegWEn), .clk(clk), .Q(ReadData1));  // open: clr
  Register #(.width(32)) x11 (.D(demultiplexer_12_out1), .en(RegWEn), .clk(clk), .Q(ReadData1));  // open: clr
  Register #(.width(32)) x10 (.D(demultiplexer_13_out1), .en(RegWEn), .clk(clk), .Q(ReadData1));  // open: clr
  Register #(.width(32)) x9 (.D(demultiplexer_14_out1), .en(RegWEn), .clk(clk), .Q(ReadData1));  // open: clr
  Register #(.width(32)) x8 (.D(demultiplexer_15_out1), .en(RegWEn), .clk(clk), .Q(ReadData1));  // open: clr
  Comparator #(.width(5)) comparator_17 (.a(5'b10000), .b(ReadIndex1), .eq(comparator_17_eq));  // open: gt, lt
  Comparator #(.width(5)) comparator_18 (.a(5'b10001), .b(ReadIndex1), .eq(comparator_18_eq));  // open: gt, lt
  Comparator #(.width(5)) comparator_19 (.a(5'b10010), .b(ReadIndex1), .eq(comparator_19_eq));  // open: gt, lt
  Comparator #(.width(5)) comparator_20 (.a(5'b10011), .b(ReadIndex1), .eq(comparator_20_eq));  // open: gt, lt
  Comparator #(.width(5)) comparator_21 (.a(5'b10100), .b(ReadIndex1), .eq(comparator_21_eq));  // open: gt, lt
  Comparator #(.width(5)) comparator_22 (.a(5'b10101), .b(ReadIndex1), .eq(comparator_22_eq));  // open: gt, lt
  Comparator #(.width(5)) comparator_23 (.a(5'b10110), .b(ReadIndex1), .eq(comparator_23_eq));  // open: gt, lt
  Comparator #(.width(5)) comparator_24 (.a(5'b10111), .b(ReadIndex1), .eq(comparator_24_eq));  // open: gt, lt
  Demultiplexer #(.width(32)) demultiplexer_16 (
    .out0(demultiplexer_16_out0), .out1(demultiplexer_16_out1), .in(WriteData), .sel(comparator_17_eq));
  Demultiplexer #(.width(32)) demultiplexer_17 (
    .out0(demultiplexer_17_out0), .out1(demultiplexer_17_out1), .in(WriteData), .sel(comparator_18_eq));
  Demultiplexer #(.width(32)) demultiplexer_18 (
    .out0(demultiplexer_18_out0), .out1(demultiplexer_18_out1), .in(WriteData), .sel(comparator_19_eq));
  Demultiplexer #(.width(32)) demultiplexer_19 (
    .out0(demultiplexer_19_out0), .out1(demultiplexer_19_out1), .in(WriteData), .sel(comparator_20_eq));
  Demultiplexer #(.width(32)) demultiplexer_20 (
    .out0(demultiplexer_20_out0), .out1(demultiplexer_20_out1), .in(WriteData), .sel(comparator_21_eq));
  Demultiplexer #(.width(32)) demultiplexer_21 (
    .out0(demultiplexer_21_out0), .out1(demultiplexer_21_out1), .in(WriteData), .sel(comparator_22_eq));
  Demultiplexer #(.width(32)) demultiplexer_22 (
    .out0(demultiplexer_22_out0), .out1(demultiplexer_22_out1), .in(WriteData), .sel(comparator_23_eq));
  Demultiplexer #(.width(32)) demultiplexer_23 (
    .out0(demultiplexer_23_out0), .out1(demultiplexer_23_out1), .in(WriteData), .sel(comparator_24_eq));
  // NoConnect on demultiplexer_16_out0
  // NoConnect on demultiplexer_17_out0
  // NoConnect on demultiplexer_18_out0
  // NoConnect on demultiplexer_19_out0
  // NoConnect on demultiplexer_20_out0
  // NoConnect on demultiplexer_21_out0
  // NoConnect on demultiplexer_22_out0
  // NoConnect on demultiplexer_23_out0
  Register #(.width(32)) x16 (.D(demultiplexer_16_out1), .en(RegWEn), .clk(clk), .Q(ReadData1));  // open: clr
  Register #(.width(32)) x17 (.D(demultiplexer_17_out1), .en(RegWEn), .clk(clk), .Q(ReadData1));  // open: clr
  Register #(.width(32)) x18 (.D(demultiplexer_18_out1), .en(RegWEn), .clk(clk), .Q(ReadData1));  // open: clr
  Register #(.width(32)) x19 (.D(demultiplexer_19_out1), .en(RegWEn), .clk(clk), .Q(ReadData1));  // open: clr
  Register #(.width(32)) x20 (.D(demultiplexer_20_out1), .en(RegWEn), .clk(clk), .Q(ReadData1));  // open: clr
  Register #(.width(32)) x21 (.D(demultiplexer_21_out1), .en(RegWEn), .clk(clk), .Q(ReadData1));  // open: clr
  Register #(.width(32)) x22 (.D(demultiplexer_22_out1), .en(RegWEn), .clk(clk), .Q(ReadData1));  // open: clr
  Register #(.width(32)) x23 (.D(demultiplexer_23_out1), .en(RegWEn), .clk(clk), .Q(ReadData1));  // open: clr
  Comparator #(.width(5)) comparator_25 (.a(5'b00001), .eq(comparator_25_eq));  // open: b, gt, lt
  Comparator #(.width(5)) comparator_26 (.a(5'b11110), .b(ReadIndex1), .eq(comparator_26_eq));  // open: gt, lt
  Comparator #(.width(5)) comparator_27 (.a(5'b11101), .b(ReadIndex1), .eq(comparator_27_eq));  // open: gt, lt
  Comparator #(.width(5)) comparator_28 (.a(5'b11100), .b(ReadIndex1), .eq(comparator_28_eq));  // open: gt, lt
  Comparator #(.width(5)) comparator_29 (.a(5'b11011), .b(ReadIndex1), .eq(comparator_29_eq));  // open: gt, lt
  Comparator #(.width(5)) comparator_30 (.a(5'b11010), .b(ReadIndex1), .eq(comparator_30_eq));  // open: gt, lt
  Comparator #(.width(5)) comparator_31 (.a(5'b11001), .b(ReadIndex1), .eq(comparator_31_eq));  // open: gt, lt
  Comparator #(.width(5)) comparator_32 (.a(5'b11000), .b(ReadIndex1), .eq(comparator_32_eq));  // open: gt, lt
  Demultiplexer #(.width(32)) demultiplexer_24 (
    .out0(demultiplexer_24_out0), .out1(demultiplexer_24_out1), .in(WriteData), .sel(comparator_25_eq));
  Demultiplexer #(.width(32)) demultiplexer_25 (
    .out0(demultiplexer_25_out0), .out1(demultiplexer_25_out1), .in(WriteData), .sel(comparator_26_eq));
  Demultiplexer #(.width(32)) demultiplexer_26 (
    .out0(demultiplexer_26_out0), .out1(demultiplexer_26_out1), .in(WriteData), .sel(comparator_27_eq));
  Demultiplexer #(.width(32)) demultiplexer_27 (
    .out0(demultiplexer_27_out0), .out1(demultiplexer_27_out1), .in(WriteData), .sel(comparator_28_eq));
  Demultiplexer #(.width(32)) demultiplexer_28 (
    .out0(demultiplexer_28_out0), .out1(demultiplexer_28_out1), .in(WriteData), .sel(comparator_29_eq));
  Demultiplexer #(.width(32)) demultiplexer_29 (
    .out0(demultiplexer_29_out0), .out1(demultiplexer_29_out1), .in(WriteData), .sel(comparator_30_eq));
  Demultiplexer #(.width(32)) demultiplexer_30 (
    .out0(demultiplexer_30_out0), .out1(demultiplexer_30_out1), .in(WriteData), .sel(comparator_31_eq));
  Demultiplexer #(.width(32)) demultiplexer_31 (
    .out0(demultiplexer_31_out0), .out1(demultiplexer_31_out1), .in(WriteData), .sel(comparator_32_eq));
  // NoConnect on demultiplexer_24_out0
  Register #(.width(32)) register_1 (.D(demultiplexer_24_out1), .en(RegWEn), .clk(clk), .Q(ReadData1));  // open: clr
  // NoConnect on demultiplexer_25_out0
  Register #(.width(32)) register_2 (.D(demultiplexer_25_out1), .en(RegWEn), .clk(clk), .Q(ReadData1));  // open: clr
  // NoConnect on demultiplexer_26_out0
  Register #(.width(32)) x29 (.D(demultiplexer_26_out1), .en(RegWEn), .clk(clk), .Q(ReadData1));  // open: clr
  // NoConnect on demultiplexer_27_out0
  Register #(.width(32)) x28 (.D(demultiplexer_27_out1), .en(RegWEn), .clk(clk), .Q(ReadData1));  // open: clr
  // NoConnect on demultiplexer_28_out0
  Register #(.width(32)) x27 (.D(demultiplexer_28_out1), .en(RegWEn), .clk(clk), .Q(ReadData1));  // open: clr
  // NoConnect on demultiplexer_29_out0
  Register #(.width(32)) x26 (.D(demultiplexer_29_out1), .en(RegWEn), .clk(clk), .Q(ReadData1));  // open: clr
  // NoConnect on demultiplexer_30_out0
  Register #(.width(32)) x25 (.D(demultiplexer_30_out1), .en(RegWEn), .clk(clk), .Q(ReadData1));  // open: clr
  // NoConnect on demultiplexer_31_out0
  Register #(.width(32)) x24 (.D(demultiplexer_31_out1), .en(RegWEn), .clk(clk), .Q(ReadData1));  // open: clr

  // Notes on the sheet:
  //   INPUTS to your circuit
  //   DON'T CHANGE THE LOCATIONS OF THE INPUTS AND OUTPUTS!
  //   These are DEBUG/TEST outputs from your circuit.
  //   OUTPUTS from your circuit
endmodule
